# Fritzing sketch Untitled Sketch (saved by Fritzing 0.9.2b)

parts:
  Componente1 = Udoo Board  # not connected
  M1 = DC Motor  # not connected
  U1 = LIPO-2000mAh [package=lipo-2000]
  U2 = LIPO-2000mAh [package=lipo-2000]
  J1 = Basic Servo  # not connected
  CONN1 = USB connector [package=THT]

nets:
  N1: U1.-, U2.+
  N2: CONN1.GND, CONN1.chassis5, CONN1.chassis6

notes:
  POLOLU SERVO BOARD
  ESC: Electronic Speed Controller
  POLOLU is connecteto to UDOO Via USB
